# Fritzing sketch final-project-diagram (saved by Fritzing 0.9.8b)
breadboards: 2

parts:
  Raspberry_Pi_2 = Raspberry Pi 4 [part_number=RPI-4-b]  # not connected
  Part1 = Arduino Uno (Rev3) - ICSP
  Part2 = adafruit
  M1 = Adafruit Anemometer [package=THT]
  J1 = Power Jack [package=power_jack_slot]
  X3 = USB Connectors [package=usb-a-pcb]
  X2 = USB Connectors [package=usb-a-pcb]

nets:
  N1: Part1.A1, M1.pin3
  GND: Part1.GND, M1.pin2, J1.GNDBREAK, J1.GND
  N2: Part2.connector12, Part2.connector13, Part2.connector14
  N3: Part2.connector17, Part2.connector19
  N4: X3.VBUS, X2.GND
  N5: X3.GND, X2.VBUS

custom parts:
  Raspberry Pi 4: The RPi4, a faster version of the awesome Raspberry Pi 2 B ARM Board with 40 pin gpio. Ready for special Raspberry Pi B+ and RPi2 Hat (Hardware attached (on) top)
  Adafruit Anemometer: Adafruit Anemometer Wind Speed Sensor w/Analog Voltage Output.
